# Fritzing sketch sensor_abfrage_pushdown (saved by Fritzing 0.9.3b)
breadboards: 1

parts:
  LED1 = LED - 5mm [color="Red (633nm)" package="5 mm [THT]"]
  S1 = Pushbutton [package="[THT]"]
  R1 = Resistor [tolerance=±5% resistance=220 package=THT]
  R2 = Resistor [tolerance=±5% resistance=220 package=THT]
  Bauteil1 = Arduino Uno (Rev3)

nets:
  N1: LED1.cathode, R2.Pin_1, Bauteil1.GND
  N2: LED1.anode, R1.Pin_1
  N3: S1.Pin_1, S1.Pin_2
  N4: S1.Pin_3, S1.Pin_4, R2.Pin_0, Bauteil1.D8, Bauteil1.5V
  N5: R1.Pin_0, Bauteil1.D13/SCK
