# Fritzing sketch blinken_mit_intervalsteuerung (saved by Fritzing 0.9.3b)
breadboards: 1

parts:
  LED1 = LED - 5mm [color="Yellow (585nm)" package="5 mm [THT]"]
  S1 = Pushbutton [package="[THT]"]
  R1 = Resistor [tolerance=±5% resistance=220 package=THT]
  R2 = Resistor [tolerance=±5% resistance=220 package=THT]
  Bauteil1 = Arduino Uno (Rev3)
  LED2 = LED - 5mm [color="Red (633nm)" package="5 mm [THT]"]
  R3 = Resistor [tolerance=±5% resistance=220 package=THT]

nets:
  N1: LED1.cathode, R2.Pin_1, Bauteil1.GND, LED2.cathode
  N2: LED1.anode, R1.Pin_1
  N3: S1.Pin_1, S1.Pin_2
  N4: S1.Pin_3, S1.Pin_4, R2.Pin_0, Bauteil1.D8, Bauteil1.5V
  N5: R1.Pin_0, Bauteil1.D10_PWM/SS
  N6: Bauteil1.D13/SCK, R3.Pin_0
  N7: LED2.anode, R3.Pin_1
